// Logisim project ALU.circ as structural Verilog: 1 circuit, main circuit main
module main (
  input  [15:0] InputA,
  input  [15:0] InputB,
  input  Clk,
  input  [3:0] ALU_OP,
  output Zero,
  output [15:0] out_6
);

  wire [0:0] or_2_out;
  wire [15:0] adder_1_out, and_1_out, InputA_q, InputB_q, or_1_out, subtractor_1_out;

  Register #(.width(16)) u_InputA (.D(InputA), .Q(InputA_q), .clk(Clk));  // open: en, clr
  Register #(.width(16)) u_InputB (.D(InputB), .Q(InputB_q), .clk(Clk));  // open: en, clr
  Adder #(.width(16)) adder_1 (.a(InputA_q), .b(InputB_q), .out(adder_1_out));  // open: cin, cout
  Subtractor #(.width(16)) subtractor_1 (.a(InputA_q), .b(InputB_q), .out(subtractor_1_out));  // open: bin, bout
  Comparator #(.width(16)) comparator_1 (.a(InputA_q), .b(InputB_q));  // open: gt, eq, lt
  assign and_1_out = InputA_q & InputB_q;  // AND_Gate and_1, 16 bits wide
  assign or_1_out = InputA_q | InputB_q;  // OR_Gate or_1, 16 bits wide
  Multiplexer #(.select(2), .width(16)) multiplexer_1 (
    .in0(adder_1_out), .in1(subtractor_1_out), .in2(and_1_out), .in3(or_1_out), .out(out_6),
    .sel({ALU_OP[1], or_2_out[0]}));  // open: en
  or or_2 (or_2_out[0], ALU_OP[2], ALU_OP[0]);
  nor nor_1 (Zero, out_6[0], out_6[1], out_6[2], out_6[3], out_6[4], out_6[5], out_6[6], out_6[7], out_6[8], out_6[9], out_6[10], out_6[11], out_6[12], out_6[13], out_6[14], out_6[15]);
  // also tied to GND on the sheet: ALU_OP[3]
endmodule
