// Logisim project ForwardingUnit.circ as structural Verilog: 1 circuit, main circuit main
// Mem/WB.RegisterWrite
module main (
  input  [2:0] Ex_Mem_RS2,
  input  [2:0] Ex_Mem_Rd,
  input  Ex_Mem_MemWrite,
  input  Mem_WB_MemToReg,
  input  Mem_WB_RegisterWrite,
  input  [2:0] ID_Ex_RS1,
  input  [2:0] Mem_WB_Rd,
  input  [2:0] ID_Ex_RS2,
  input  Ex_Mem_RegisterWrite,
  output C,
  output A,
  output B
);

  wire and_1_out, and_5_out, and_6_out, comparator_1_eq, comparator_2_eq, comparator_3_eq, comparator_4_eq,
       comparator_5_eq, comparator_6_eq, comparator_7_eq, comparator_8_eq, comparator_9_eq, not_1_out,
       not_2_out, not_3_out, not_4_out, not_5_out, not_6_out;

  Comparator #(.width(3)) comparator_1 (.a(ID_Ex_RS1), .b(3'b000), .eq(comparator_1_eq));  // open: gt, lt
  Comparator #(.width(3)) comparator_2 (.a(Ex_Mem_Rd), .b(ID_Ex_RS1), .eq(comparator_2_eq));  // open: gt, lt
  Comparator #(.width(3)) comparator_3 (.a(ID_Ex_RS1), .b(3'b000), .eq(comparator_3_eq));  // open: gt, lt
  Comparator #(.width(3)) comparator_4 (.a(Mem_WB_Rd), .b(ID_Ex_RS1), .eq(comparator_4_eq));  // open: gt, lt
  Comparator #(.width(3)) comparator_5 (.a(ID_Ex_RS2), .b(3'b000), .eq(comparator_5_eq));  // open: gt, lt
  Comparator #(.width(3)) comparator_6 (.a(Ex_Mem_Rd), .b(ID_Ex_RS2), .eq(comparator_6_eq));  // open: gt, lt
  Comparator #(.width(3)) comparator_7 (.a(ID_Ex_RS2), .b(3'b000), .eq(comparator_7_eq));  // open: gt, lt
  Comparator #(.width(3)) comparator_8 (.a(Mem_WB_Rd), .b(ID_Ex_RS2), .eq(comparator_8_eq));  // open: gt, lt
  not not_1 (not_1_out, comparator_1_eq);
  not not_2 (not_2_out, comparator_3_eq);
  not not_3 (not_3_out, comparator_5_eq);
  not not_4 (not_4_out, comparator_7_eq);
  Comparator #(.width(3)) comparator_9 (.a(Ex_Mem_RS2), .b(Ex_Mem_Rd), .eq(comparator_9_eq));  // open: gt, lt
  and and_1 (and_1_out, Ex_Mem_MemWrite, Mem_WB_MemToReg);
  and and_2 (A, Ex_Mem_RegisterWrite, not_1_out, comparator_2_eq);
  and and_3 (B, Ex_Mem_RegisterWrite, not_3_out, comparator_6_eq);
  and and_4 (C, comparator_9_eq, and_1_out);
  not not_5 (not_5_out, A);
  and and_5 (and_5_out, not_5_out, Mem_WB_RegisterWrite, not_2_out, comparator_4_eq);
  not not_6 (not_6_out, B);
  and and_6 (and_6_out, not_6_out, Mem_WB_RegisterWrite, not_4_out, comparator_8_eq);
endmodule
