// Logisim project HazardControlUnit.circ as structural Verilog: 1 circuit, main circuit main
module main (
  input  PCSrc,
  input  ID_Ex_MemRead,
  input  [2:0] ID_Ex_Rd,
  input  [2:0] IF_ID_RS1,
  input  [2:0] IF_ID_RS2,
  output Stall,
  output Flush
);

  wire comparator_1_eq, comparator_2_eq, ID_Ex_MemRead_t, or_1_out;

  Comparator #(.width(3)) comparator_1 (.a(ID_Ex_Rd), .b(IF_ID_RS1), .eq(comparator_1_eq));  // open: gt, lt
  Comparator #(.width(3)) comparator_2 (.a(ID_Ex_Rd), .b(IF_ID_RS2), .eq(comparator_2_eq));  // open: gt, lt
  or or_1 (or_1_out, comparator_1_eq, comparator_2_eq);
  and and_1 (Stall, ID_Ex_MemRead_t, or_1_out);

  assign Flush = PCSrc;
endmodule
