// Logisim project IF-ID_Buffer.circ as structural Verilog: 1 circuit, main circuit main
module main (
  input  [15:0] Instruction,
  input  IF_ID_Enable,
  input  Clk,
  output [3:0] Opcode,
  output [2:0] ReadRegister1,
  output [2:0] ReadRegister2,
  output [2:0] WriteRegister,
  output [3:0] ShiftAmount,
  output SubOp,
  output Unsigned,
  output [7:0] Immediate
);

  Register #(.width(16)) Buffer (
    .D(Instruction), .en(IF_ID_Enable), .Q({Opcode, ReadRegister1, ReadRegister2[2], Immediate}), .clk(Clk));  // open: clr

  assign ReadRegister2[1:0] = Immediate[7:6];
  assign ShiftAmount = Immediate[4:1];
  assign SubOp = Immediate[0];
  assign Unsigned = ReadRegister2[2];
  assign WriteRegister = ReadRegister1;
endmodule
