// Logisim project LED_Hex_Display.circ as structural Verilog: 1 circuit, main circuit main
module main (
  input  [15:0] DataIn,
  input  Put,
  input  Clk
);

  wire [3:0] register_2_q_2;
  wire [11:0] register_2_q;
  wire [15:0] register_1_q;

  Register #(.width(16)) register_1 (.D(DataIn), .Q(register_1_q), .clk(Clk));  // open: en, clr
  Hex_Digit_Display hex_digit_display_1 (.value(register_2_q_2));  // open: dp
  Hex_Digit_Display hex_digit_display_2 (.value(register_2_q[11:8]));  // open: dp
  Register #(.width(16)) register_2 (
    .D(register_1_q), .en(Put), .Q({register_2_q_2, register_2_q}), .clk(Clk));  // open: clr
  Hex_Digit_Display hex_digit_display_3 (.value(register_2_q[7:4]));  // open: dp
  Hex_Digit_Display hex_digit_display_4 (.value(register_2_q[3:0]));  // open: dp
endmodule
