// Logisim project Register_File.circ as structural Verilog: 1 circuit, main circuit main
module main (
  output [2:0] ReadRegister1,
  output [2:0] ReadRegister2,
  output [2:0] WriteRegister,
  output [15:0] ReadData1,
  output [15:0] WriteData,
  output [15:0] ReadData2,
  output WriteEnable,
  output Clk
);

  wire decoder_1_out0, decoder_1_out1, decoder_1_out2, decoder_1_out3, decoder_1_out4, decoder_1_out5,
       decoder_1_out6, decoder_1_out7;
  wire [15:0] r0_q, r1_q, r2_q, r3_q, r4_q, r5_q, r6_q, r7_q;

  Decoder #(.select(3)) decoder_1 (
    .out0(decoder_1_out0), .out1(decoder_1_out1), .out2(decoder_1_out2), .out3(decoder_1_out3),
    .out4(decoder_1_out4), .out5(decoder_1_out5), .out6(decoder_1_out6), .out7(decoder_1_out7),
    .sel(WriteRegister), .en(WriteEnable));
  Register #(.width(16)) r0 (.D(WriteData), .en(decoder_1_out0), .Q(r0_q), .clk(Clk));  // open: clr
  Register #(.width(16)) r1 (.D(WriteData), .en(decoder_1_out1), .Q(r1_q), .clk(Clk));  // open: clr
  Register #(.width(16)) r2 (.D(WriteData), .en(decoder_1_out2), .Q(r2_q), .clk(Clk));  // open: clr
  Register #(.width(16)) r3 (.D(WriteData), .en(decoder_1_out3), .Q(r3_q), .clk(Clk));  // open: clr
  Register #(.width(16)) r4 (.D(WriteData), .en(decoder_1_out4), .Q(r4_q), .clk(Clk));  // open: clr
  Register #(.width(16)) r5 (.D(WriteData), .en(decoder_1_out5), .Q(r5_q), .clk(Clk));  // open: clr
  Register #(.width(16)) r6 (.D(WriteData), .en(decoder_1_out6), .Q(r6_q), .clk(Clk));  // open: clr
  Register #(.width(16)) r7 (.D(WriteData), .en(decoder_1_out7), .Q(r7_q), .clk(Clk));  // open: clr
  Multiplexer #(.select(3), .width(16), .enable("false")) multiplexer_1 (
    .in0(r0_q), .in1(r1_q), .in2(r2_q), .in3(r3_q), .in4(r4_q), .in5(r5_q), .in6(r6_q), .in7(r7_q),
    .out(ReadData1), .sel(ReadRegister1));
  Multiplexer #(.select(3), .width(16), .enable("false")) multiplexer_2 (
    .in0(r0_q), .in1(r1_q), .in2(r2_q), .in3(r3_q), .in4(r4_q), .in5(r5_q), .in6(r6_q), .in7(r7_q),
    .out(ReadData2), .sel(ReadRegister2));
endmodule
