// Logisim project main.circ as structural Verilog: 1 circuit, main circuit main
module main (
  input  [1:0] A,
  input  [2:0] ReadRegister1,
  input  [15:0] ReadData1,
  input  [2:0] ReadRegister2,
  input  [2:0] WriteRegister,
  input  [15:0] ReadData2,
  input  [15:0] WriteData,
  input  ALUSrc,
  input  [1:0] B,
  input  ALUOp,
  input  [15:0] Imm,
  input  [15:0] Instruction_ImmGen,
  output [15:0] ReadData1_2,
  output [15:0] Instruction,
  output [15:0] ReadData2_2,
  output [31:0] Immediate
);

  wire Clk;
  wire [7:0] PC;
  wire [15:0] ALU_Result, MemoryResult, multiplexer_1_out, multiplexer_2_out, multiplexer_3_out;

  Clock clock_1 (.out(Clk));
  ROM #(.dataWidth(16)) rom_1 (.addr(PC), .data(Instruction));  // open: sel
  assign Immediate = {{16{Instruction_ImmGen[15]}}, Instruction_ImmGen};  // Bit_Extender bit_extender_1
  Register_File_main main_1 (
    .ReadRegister1(ReadRegister1), .ReadRegister2(ReadRegister2), .WriteRegister(WriteRegister),
    .WriteData(WriteData), .WriteEnable(ALUOp), .Clk(Clk), .ReadData1(ReadData1_2), .ReadData2(ReadData2_2));
  Multiplexer #(.select(2), .width(16)) multiplexer_1 (
    .in0(ReadData1), .in1(MemoryResult), .in2(ALU_Result), .in3({16{1'b0}}), .out(multiplexer_1_out), .sel(A));  // open: en
  Multiplexer #(.select(2), .width(16)) multiplexer_2 (
    .in0(ReadData2), .in1(MemoryResult), .in2(ALU_Result), .in3({16{1'b0}}), .out(multiplexer_2_out), .sel(B));  // open: en
  Multiplexer #(.width(16)) multiplexer_3 (
    .in0(multiplexer_2_out), .in1(Imm), .out(multiplexer_3_out), .sel(ALUSrc));  // open: en

  // Notes on the sheet:
  //   Instruction Memory
  //   Clock!
  //   IF/ID
  //   This feels like the wrong in/out size
  //   Imm Gen
  //   Registers
  //   ID/EX
endmodule
