// Logisim project pipelinecircuit.circ as structural Verilog: 25 circuits, main circuit main
module main (
);

  wire and_1_out, button_1_out, Clock, comparator_1_eq, comparator_2_eq, comparator_2_lt, Decoder_immtopc,
       Decoder_led, EX_MEM_Register_ex_mem_memread, EX_MEM_Register_ex_mem_memtoreg,
       EX_MEM_Register_ex_mem_memwrite, EX_MEM_Register_ex_mem_writeenable, Flush, FwdC, FwdD, FwdE, Halt,
       ID_EX_MemRead, ID_EX_Register_id_ex_alusrc, ID_EX_Register_id_ex_memtoreg,
       ID_EX_Register_id_ex_memwrite, ID_EX_Register_id_ex_writeenable, ID_EX_Register_id_ex_writeled,
       IF_ID_MemWrite, Instruction_Splitter_subop, Instruction_Splitter_unsigned,
       MEM_WB_Register_mem_wb_memtoreg, MEM_WB_WriteEnable, not_1_out, or_1_out, Stall;
  wire [1:0] FwdA, FwdB;
  wire [2:0] EX_MEM_Register_ex_mem_writeregister, ID_EX_Register_id_ex_rs1, ID_EX_Register_id_ex_rs2,
       ID_EX_Register_id_ex_writeregister, IF_ID_RS1, IF_ID_RS2, Instruction_Splitter_writeregister,
       MEM_WB_WriteRegister;
  wire [3:0] Decoder_aluop, ID_EX_Register_id_ex_aluop, Instruction_Splitter_opcode;
  wire [5:0] Decoder_immtoalu;
  wire [7:0] adder_1_out, Instruction_Splitter_immediate, multiplexer_4_out, PC_q, RegisterToAddress_address;
  wire [9:0] multiplexer_5_out;
  wire [15:0] ALU_result, EX_MEM_Register_ex_mem_readdata1, EX_MEM_Register_ex_mem_readdata2,
       EX_MEM_Register_ex_mem_result, ID_EX_Register_id_ex_readdata1, ID_EX_Register_id_ex_readdata2,
       ID_EX_Register_id_ex_signextimm, IF_ID_Register_q, MEM_WB_Register_mem_wb_memdata,
       MEM_WB_Register_mem_wb_result, MEM_WB_WriteData, multiplexer_1_out, multiplexer_2_out,
       multiplexer_3_out, multiplexer_6_out, multiplexer_7_out, multiplexer_8_out, multiplexer_9_out,
       multiplexer_10_out, ram_1_data, Register_File_readdata1, Register_File_readdata2, rom_1_data,
       Sign_Extend_signextendedimm;

  Clock clock_1 (.out(Clock));
  Comparator comparator_1 (.a(PC_q), .b({8{1'b0}}), .eq(comparator_1_eq));  // open: gt, lt
  Register PC (.D(multiplexer_4_out), .en(not_1_out), .Q(PC_q), .clk(Clock), .clr(button_1_out));
  Button button_1 (.out(button_1_out));
  not not_1 (not_1_out, or_1_out);
  or or_1 (or_1_out, Halt, and_1_out);
  and and_1 (and_1_out, ~comparator_1_eq, Stall);  // AND_Gate
  Adder adder_1 (.a(PC_q), .b(8'h1), .out(adder_1_out));  // open: cin, cout
  ROM #(.dataWidth(16)) rom_1 (.addr(PC_q), .data(rom_1_data), .sel(1'b1));
  Multiplexer #(.width(16), .enable("false")) multiplexer_1 (
    .in0(rom_1_data), .in1({16{1'b0}}), .out(multiplexer_1_out), .sel(Flush));
  Register #(.width(16)) IF_ID_Register (
    .D(multiplexer_1_out), .en(not_1_out), .Q(IF_ID_Register_q), .clk(Clock));  // open: clr
  InstructionSplitter Instruction_Splitter (
    .Instruction(IF_ID_Register_q), .Opcode(Instruction_Splitter_opcode), .ReadRegister1(IF_ID_RS1),
    .ReadRegister2(IF_ID_RS2), .WriteRegister(Instruction_Splitter_writeregister),
    .SubOp(Instruction_Splitter_subop), .Unsigned(Instruction_Splitter_unsigned),
    .Immediate(Instruction_Splitter_immediate));  // open: ShiftAmount
  Comparator #(.width(16)) comparator_2 (
    .a(Register_File_readdata1), .b({16{1'b0}}), .eq(comparator_2_eq), .lt(comparator_2_lt));  // open: gt
  Decoder Decoder (
    .Opcode(Instruction_Splitter_opcode), .Subop(Instruction_Splitter_subop), .Zero(comparator_2_eq),
    .Less(comparator_2_lt), .RegWrite(Decoder_immtoalu[4]), .ALUOp(Decoder_aluop),
    .IMMtoALU(Decoder_immtoalu[0]), .IMMtoPC(Decoder_immtopc), .MemWrite(IF_ID_MemWrite),
    .MemtoReg(Decoder_immtoalu[2]), .Halt(Halt), .LED(Decoder_led), .WriteLED(Decoder_immtoalu[5]),
    .MemRead(Decoder_immtoalu[3]));  // open: ShiftSrc, ShifterToReg, RegtoPC, ZerosToALU, PCtoReg
  RegisterFile Register_File (
    .ReadRegister1(IF_ID_RS1), .ReadRegister2(IF_ID_RS2), .WriteRegister(MEM_WB_WriteRegister),
    .WriteData(MEM_WB_WriteData), .WriteEnable(MEM_WB_WriteEnable), .Clock(Clock),
    .ReadData1(Register_File_readdata1), .ReadData2(Register_File_readdata2));
  LED u_Halt (.in(Decoder_led));
  SignExtend Sign_Extend (
    .Unsigned(Instruction_Splitter_unsigned), .Immediate(Instruction_Splitter_immediate),
    .SignExtendedImm(Sign_Extend_signextendedimm));
  Multiplexer #(.width(16), .enable("false")) multiplexer_2 (
    .in0(Register_File_readdata1), .in1(MEM_WB_WriteData), .out(multiplexer_2_out), .sel(FwdD));
  Multiplexer #(.width(16), .enable("false")) multiplexer_3 (
    .in0(Register_File_readdata2), .in1(MEM_WB_WriteData), .out(multiplexer_3_out), .sel(FwdE));
  Multiplexer #(.width(8), .enable("false")) multiplexer_4 (
    .in0(adder_1_out), .in1(Instruction_Splitter_immediate), .out(multiplexer_4_out), .sel(Decoder_immtopc));
  Multiplexer #(.width(10), .enable("false")) multiplexer_5 (
    .in0({Decoder_immtoalu[5:2], IF_ID_MemWrite, Decoder_immtoalu[0], Decoder_aluop}), .in1({10{1'b0}}),
    .out(multiplexer_5_out), .sel(Stall));
  ID_EX_Register ID_EX_Register (
    .ReadData1(multiplexer_2_out), .ReadData2(multiplexer_3_out), .Clock(Clock), .ID_EX_En(1'b1),
    .WriteRegister(Instruction_Splitter_writeregister), .SignExtImm(Sign_Extend_signextendedimm),
    .ALUOp(multiplexer_5_out[3:0]), .IF_ID_ControlSignals(multiplexer_5_out[9:4]), .Rs1(IF_ID_RS1),
    .Rs2(IF_ID_RS2), .ID_EX_ReadData1(ID_EX_Register_id_ex_readdata1),
    .ID_EX_ReadData2(ID_EX_Register_id_ex_readdata2),
    .ID_EX_WriteRegister(ID_EX_Register_id_ex_writeregister),
    .ID_EX_SignExtImm(ID_EX_Register_id_ex_signextimm), .ID_EX_ALUOp(ID_EX_Register_id_ex_aluop),
    .ID_EX_ALUSrc(ID_EX_Register_id_ex_alusrc), .ID_EX_MemWrite(ID_EX_Register_id_ex_memwrite),
    .ID_EX_MemRead(ID_EX_MemRead), .ID_EX_MemToReg(ID_EX_Register_id_ex_memtoreg),
    .ID_EX_WriteEnable(ID_EX_Register_id_ex_writeenable), .ID_EX_WriteLED(ID_EX_Register_id_ex_writeled),
    .ID_EX_Rs1(ID_EX_Register_id_ex_rs1), .ID_EX_Rs2(ID_EX_Register_id_ex_rs2));
  HazardControlUnit hazardcontrolunit_1 (
    .IF_ID_MemWrite(IF_ID_MemWrite), .ALUSrc(Decoder_immtoalu[0]), .PCSrc(Decoder_immtopc),
    .ID_Ex_MemRead(ID_EX_MemRead), .ID_Ex_Rd(ID_EX_Register_id_ex_writeregister), .IF_ID_RS1(IF_ID_RS1),
    .IF_ID_RS2(IF_ID_RS2), .Mem_WB_Rd(MEM_WB_WriteRegister), .Stall(Stall), .Flush(Flush));
  Multiplexer #(.select(2), .width(16), .enable("false")) multiplexer_6 (
    .in0(ID_EX_Register_id_ex_readdata1), .in1(MEM_WB_WriteData), .in2(EX_MEM_Register_ex_mem_result),
    .out(multiplexer_6_out), .sel(FwdA));  // open: in3
  Multiplexer #(.select(2), .width(16), .enable("false")) multiplexer_7 (
    .in0(ID_EX_Register_id_ex_readdata2), .in1(MEM_WB_WriteData), .in2(EX_MEM_Register_ex_mem_result),
    .out(multiplexer_7_out), .sel(FwdB));  // open: in3
  Multiplexer #(.width(16), .disabled(0), .enable("false")) multiplexer_8 (
    .in0(multiplexer_7_out), .in1(ID_EX_Register_id_ex_signextimm), .out(multiplexer_8_out),
    .sel(ID_EX_Register_id_ex_alusrc));
  Multiplexer #(.width(16), .enable("false")) multiplexer_9 (
    .in0({16{1'b0}}), .in1(ID_EX_Register_id_ex_readdata1), .out(multiplexer_9_out),
    .sel(ID_EX_Register_id_ex_writeled));
  sixteen_bit_ALU ALU (
    .ALUOperation(ID_EX_Register_id_ex_aluop), .a(multiplexer_6_out), .b(multiplexer_8_out),
    .Result(ALU_result));  // open: Zero, Overflow
  Hex_Digit_Display hex_digit_display_1 (.value(multiplexer_9_out[15:12]));  // open: dp
  Hex_Digit_Display hex_digit_display_2 (.value(multiplexer_9_out[11:8]));  // open: dp
  Hex_Digit_Display hex_digit_display_3 (.value(multiplexer_9_out[7:4]));  // open: dp
  EX_MEM_Register EX_MEM_Register (
    .Clock(Clock), .EX_MEM_En(1'b1), .Result(ALU_result), .WriteRegister(ID_EX_Register_id_ex_writeregister),
    .ReadData2(ID_EX_Register_id_ex_readdata2), .MemWrite(ID_EX_Register_id_ex_memwrite),
    .MemRead(ID_EX_MemRead), .MemToReg(ID_EX_Register_id_ex_memtoreg),
    .WriteEnable(ID_EX_Register_id_ex_writeenable), .Rs2(ID_EX_Register_id_ex_rs2),
    .ReadData1(multiplexer_6_out), .EX_MEM_Result(EX_MEM_Register_ex_mem_result),
    .EX_MEM_WriteRegister(EX_MEM_Register_ex_mem_writeregister),
    .EX_MEM_ReadData2(EX_MEM_Register_ex_mem_readdata2), .EX_MEM_MemWrite(EX_MEM_Register_ex_mem_memwrite),
    .EX_MEM_MemRead(EX_MEM_Register_ex_mem_memread), .EX_MEM_MemToReg(EX_MEM_Register_ex_mem_memtoreg),
    .EX_MEM_WriteEnable(EX_MEM_Register_ex_mem_writeenable),
    .EX_MEM_ReadData1(EX_MEM_Register_ex_mem_readdata1));  // open: EX_MEM_Rs2
  Hex_Digit_Display hex_digit_display_4 (.value(multiplexer_9_out[3:0]));  // open: dp
  ALUtoPC RegisterToAddress (.ALUOut(EX_MEM_Register_ex_mem_readdata2), .Address(RegisterToAddress_address));
  ForwardingUnit Forwarding_Unit (
    .Ex_Mem_RS1(EX_MEM_Register_ex_mem_writeregister), .Ex_Mem_Rd(EX_MEM_Register_ex_mem_writeregister),
    .Ex_Mem_MemWrite(EX_MEM_Register_ex_mem_memwrite), .IF_ID_RS1(IF_ID_RS1),
    .Mem_WB_MemToReg(MEM_WB_Register_mem_wb_memtoreg), .IF_ID_RS2(IF_ID_RS2),
    .Mem_WB_RegisterWrite(MEM_WB_WriteEnable), .ID_Ex_RS1(ID_EX_Register_id_ex_rs1),
    .Mem_WB_Rd(MEM_WB_WriteRegister), .ID_Ex_RS2(ID_EX_Register_id_ex_rs2),
    .Ex_Mem_RegisterWrite(EX_MEM_Register_ex_mem_writeenable), .C(FwdC), .D(FwdD), .E(FwdE), .A(FwdA),
    .B(FwdB));
  Multiplexer #(.width(16), .enable("false")) multiplexer_10 (
    .in0(EX_MEM_Register_ex_mem_readdata1), .in1(MEM_WB_Register_mem_wb_memdata), .out(multiplexer_10_out),
    .sel(FwdC));
  RAM #(.dataWidth(16), .bus("separate")) ram_1 (
    .addr(RegisterToAddress_address), .din(multiplexer_10_out), .data(ram_1_data),
    .str(EX_MEM_Register_ex_mem_memwrite), .sel(1'b1), .clk(Clock), .ld(EX_MEM_Register_ex_mem_memread));  // open: clr
  MEM_WB_Register MEM_WB_Register (
    .Clock(Clock), .EX_MEM_WriteRegister(EX_MEM_Register_ex_mem_writeregister),
    .Result(EX_MEM_Register_ex_mem_result), .EX_MEM_MemData(ram_1_data),
    .MemToReg(EX_MEM_Register_ex_mem_memtoreg), .WriteEnable(EX_MEM_Register_ex_mem_writeenable),
    .MEM_WB_WriteRegister(MEM_WB_WriteRegister), .MEM_WB_Result(MEM_WB_Register_mem_wb_result),
    .MEM_WB_MemData(MEM_WB_Register_mem_wb_memdata), .MEM_WB_MemToReg(MEM_WB_Register_mem_wb_memtoreg),
    .MEM_WB_WriteEnable(MEM_WB_WriteEnable));
  Multiplexer #(.width(16), .disabled(0), .enable("false")) multiplexer_11 (
    .in0(MEM_WB_Register_mem_wb_result), .in1(MEM_WB_Register_mem_wb_memdata), .out(MEM_WB_WriteData),
    .sel(MEM_WB_Register_mem_wb_memtoreg));

  // Notes on the sheet:
  //   contents of rom_1 (hex, n*v repeats v):
  //   280 8604 280 280 700 280 b80 f600 7000
endmodule

module InstructionSplitter (
  input  [15:0] Instruction,
  output [3:0] Opcode,
  output [2:0] ReadRegister1,
  output [2:0] ReadRegister2,
  output [2:0] WriteRegister,
  output [3:0] ShiftAmount,
  output SubOp,
  output Unsigned,
  output [7:0] Immediate
);


  assign Immediate = Instruction[7:0];
  assign Opcode = Instruction[15:12];
  assign ReadRegister1 = Instruction[11:9];
  assign ReadRegister2 = Instruction[8:6];
  assign ShiftAmount = Instruction[4:1];
  assign SubOp = Instruction[0];
  assign Unsigned = Instruction[8];
  assign WriteRegister = Instruction[11:9];
endmodule

module SignExtend (
  input  Unsigned,
  input  [7:0] Immediate,
  output [15:0] SignExtendedImm
);

  wire [15:0] bit_extender_1_out, bit_extender_2_out;

  assign bit_extender_1_out = {{8{Immediate[7]}}, Immediate};  // Bit_Extender bit_extender_1
  assign bit_extender_2_out = {{8{1'b0}}, Immediate};  // Bit_Extender bit_extender_2
  Multiplexer #(.width(16), .disabled(0), .enable("false")) multiplexer_1 (
    .in0(bit_extender_1_out), .in1(bit_extender_2_out), .out(SignExtendedImm), .sel(Unsigned));
endmodule

module ALUtoPC (
  input  [15:0] ALUOut,
  output [7:0] Address
);


  assign Address = ALUOut[7:0];
endmodule

module Shifter (
  input  Subop,
  input  [15:0] Data,
  input  [15:0] ShamtReg,
  input  ShiftSrc,
  input  [3:0] Shamt,
  output [15:0] ShiftOut
);

  wire [3:0] multiplexer_1_out;
  wire [15:0] shifter_1_out, shifter_2_out;

  Multiplexer #(.width(4), .disabled(0), .enable("false")) multiplexer_1 (
    .in0(ShamtReg[3:0]), .in1(Shamt), .out(multiplexer_1_out), .sel(ShiftSrc));
  Shifter_part #(.width(16)) shifter_1 (.in(Data), .\dist (multiplexer_1_out), .out(shifter_1_out));
  Shifter_part #(.width(16), .shift("lr")) shifter_2 (.in(Data), .\dist (multiplexer_1_out), .out(shifter_2_out));
  Multiplexer #(.width(16), .disabled(0), .enable("false")) multiplexer_2 (
    .in0(shifter_1_out), .in1(shifter_2_out), .out(ShiftOut), .sel(Subop));
endmodule

module RegisterFile (
  input  [2:0] ReadRegister1,
  input  [2:0] ReadRegister2,
  input  [2:0] WriteRegister,
  input  [15:0] WriteData,
  input  WriteEnable,
  input  Clock,
  output [15:0] ReadData1,
  output [15:0] ReadData2
);

  wire decoder_1_out0, decoder_1_out1, decoder_1_out2, decoder_1_out3, decoder_1_out4, decoder_1_out5,
       decoder_1_out6, decoder_1_out7;
  wire [15:0] register_1_q, register_2_q, register_3_q, register_4_q, register_5_q, register_6_q,
       register_7_q, register_8_q;

  Decoder_part #(.select(3), .disabled(0)) decoder_1 (
    .out0(decoder_1_out0), .out1(decoder_1_out1), .out2(decoder_1_out2), .out3(decoder_1_out3),
    .out4(decoder_1_out4), .out5(decoder_1_out5), .out6(decoder_1_out6), .out7(decoder_1_out7),
    .sel(WriteRegister), .en(WriteEnable));
  Register #(.width(16)) register_1 (.D(WriteData), .en(decoder_1_out0), .Q(register_1_q), .clk(Clock));  // open: clr
  Register #(.width(16)) register_2 (.D(WriteData), .en(decoder_1_out1), .Q(register_2_q), .clk(Clock));  // open: clr
  Register #(.width(16)) register_3 (.D(WriteData), .en(decoder_1_out2), .Q(register_3_q), .clk(Clock));  // open: clr
  Register #(.width(16)) register_4 (.D(WriteData), .en(decoder_1_out3), .Q(register_4_q), .clk(Clock));  // open: clr
  Register #(.width(16)) register_5 (.D(WriteData), .en(decoder_1_out4), .Q(register_5_q), .clk(Clock));  // open: clr
  Register #(.width(16)) register_6 (.D(WriteData), .en(decoder_1_out5), .Q(register_6_q), .clk(Clock));  // open: clr
  Register #(.width(16)) register_7 (.D(WriteData), .en(decoder_1_out6), .Q(register_7_q), .clk(Clock));  // open: clr
  Register #(.width(16)) register_8 (.D(WriteData), .en(decoder_1_out7), .Q(register_8_q), .clk(Clock));  // open: clr
  Multiplexer #(.select(3), .width(16), .enable("false")) multiplexer_1 (
    .in0(register_1_q), .in1(register_2_q), .in2(register_3_q), .in3(register_4_q), .in4(register_5_q),
    .in5(register_6_q), .in6(register_7_q), .in7(register_8_q), .out(ReadData1), .sel(ReadRegister1));
  Multiplexer #(.select(3), .width(16), .enable("false")) multiplexer_2 (
    .in0(register_1_q), .in1(register_2_q), .in2(register_3_q), .in3(register_4_q), .in4(register_5_q),
    .in5(register_6_q), .in6(register_7_q), .in7(register_8_q), .out(ReadData2), .sel(ReadRegister2));
endmodule

module ShifterDecoder (
  input  [3:0] Opcode,
  output ShiftSrc,
  output ShiftertoReg,
  output RegWrite
);

  and and_1 (RegWrite, ~Opcode[3], Opcode[2], ~Opcode[1]);  // AND_Gate

  assign ShiftertoReg = RegWrite;
  assign ShiftSrc = Opcode[0];
endmodule

module Arith_Log_Decoder (
  input  [3:0] Opcode,
  input  Subop,
  output [3:0] ALUOperation,
  output RegWrite,
  output ALUSrc
);

  wire and_1_out, and_3_out, and_4_out, and_5_out, and_6_out, and_7_out, not_1_out, not_2_out, not_3_out,
       not_4_out, not_5_out, not_6_out, not_7_out, not_8_out, not_9_out, not_10_out, not_11_out, not_12_out,
       not_13_out, not_14_out, not_15_out, not_16_out, not_17_out, not_18_out, not_19_out, not_20_out,
       not_21_out, not_22_out, not_23_out, not_24_out;

  not not_1 (not_1_out, Opcode[3]);
  not not_2 (not_2_out, Opcode[2]);
  not not_3 (not_3_out, Opcode[0]);
  not not_4 (not_4_out, Opcode[3]);
  not not_5 (not_5_out, Opcode[2]);
  not not_6 (not_6_out, Subop);
  not not_7 (not_7_out, Opcode[3]);
  not not_8 (not_8_out, Opcode[2]);
  not not_9 (not_9_out, Opcode[1]);
  not not_10 (not_10_out, Opcode[0]);
  not not_11 (not_11_out, Opcode[3]);
  not not_12 (not_12_out, Opcode[2]);
  not not_13 (not_13_out, Subop);
  not not_14 (not_14_out, Opcode[3]);
  not not_15 (not_15_out, Opcode[2]);
  not not_16 (not_16_out, Opcode[1]);
  not not_17 (not_17_out, Opcode[3]);
  not not_18 (not_18_out, Opcode[2]);
  not not_19 (not_19_out, Opcode[1]);
  not not_20 (not_20_out, Opcode[3]);
  not not_21 (not_21_out, Opcode[2]);
  not not_22 (not_22_out, Opcode[3]);
  not not_23 (not_23_out, Opcode[2]);
  not not_24 (not_24_out, Opcode[1]);
  and and_1 (and_1_out, not_1_out, not_2_out, not_3_out, Opcode[1]);
  and and_2 (ALUOperation[3], not_4_out, not_5_out, Opcode[1], Opcode[0], not_6_out);
  and and_3 (and_3_out, not_7_out, not_8_out, not_9_out, not_10_out, Subop);
  and and_4 (and_4_out, not_11_out, not_12_out, Opcode[1], Opcode[0], not_13_out);
  and and_5 (and_5_out, not_14_out, not_15_out, not_16_out);
  and and_6 (and_6_out, not_17_out, not_18_out, not_19_out);
  and and_7 (and_7_out, not_20_out, not_21_out, Opcode[0]);
  and and_8 (ALUSrc, not_22_out, not_23_out, not_24_out, Opcode[0]);
  or or_1 (ALUOperation[2], and_3_out, and_1_out, and_4_out);
  or or_2 (ALUOperation[1], and_1_out, and_5_out);
  or or_3 (RegWrite, and_6_out, and_1_out, and_7_out);

  assign ALUOperation[0] = 1'b0;
endmodule

module Arith_Log (
  input  Opcode3,
  input  Opcode2,
  input  Opcode1,
  input  Opcode0,
  input  Unsigned,
  input  Subop,
  output ALUOp3,
  output ALUOp2,
  output ALUOp1,
  output ALUOp0,
  output RegWrite,
  output ALUSrc
);

  wire and_2_out, and_3_out, and_5_out, and_6_out, not_1_out, not_2_out, not_3_out, not_4_out, not_5_out,
       not_6_out, not_7_out, not_8_out, not_9_out, not_10_out, not_11_out, not_12_out, not_13_out,
       not_14_out, not_15_out, not_16_out, not_17_out, not_18_out, not_19_out, not_20_out, not_21_out;

  not not_1 (not_1_out, Opcode3);
  not not_2 (not_2_out, Opcode2);
  not not_3 (not_3_out, Subop);
  not not_4 (not_4_out, Opcode3);
  not not_5 (not_5_out, Opcode2);
  not not_6 (not_6_out, Opcode1);
  not not_7 (not_7_out, Opcode0);
  not not_8 (not_8_out, Opcode3);
  not not_9 (not_9_out, Opcode2);
  not not_10 (not_10_out, Subop);
  not not_11 (not_11_out, Opcode3);
  not not_12 (not_12_out, Opcode2);
  not not_13 (not_13_out, Opcode1);
  not not_14 (not_14_out, Opcode3);
  not not_15 (not_15_out, Opcode2);
  not not_16 (not_16_out, Opcode1);
  not not_17 (not_17_out, Opcode3);
  not not_18 (not_18_out, Opcode2);
  not not_19 (not_19_out, Opcode3);
  not not_20 (not_20_out, Opcode2);
  not not_21 (not_21_out, Opcode1);
  and and_1 (ALUOp3, not_1_out, not_2_out, Opcode1, Opcode0, not_3_out);
  and and_2 (and_2_out, not_4_out, not_5_out, not_6_out, not_7_out, Subop);
  and and_3 (and_3_out, not_8_out, not_9_out, Opcode1, Opcode0, not_10_out);
  and and_4 (ALUOp1, not_11_out, not_12_out, not_13_out);
  and and_5 (and_5_out, not_14_out, not_15_out, not_16_out);
  and and_6 (and_6_out, not_17_out, not_18_out, Opcode0);
  and and_7 (ALUSrc, not_19_out, not_20_out, not_21_out, Opcode0);
  or or_1 (ALUOp2, and_2_out, and_3_out);
  or or_2 (RegWrite, and_5_out, and_6_out);

  assign ALUOp0 = 1'b0;
endmodule

module one_bit_ALU (
  input  Ainvert,
  input  Binvert,
  input  CarryIn,
  input  [1:0] Operation,
  input  a,
  input  b,
  input  Less,
  output Result,
  output Set,
  output CarryOut
);

  wire and_1_out, multiplexer_1_out, multiplexer_2_out, not_1_out, not_2_out, or_1_out;

  not not_1 (not_1_out, a);
  Multiplexer #(.enable("false")) multiplexer_1 (.in0(a), .in1(not_1_out), .out(multiplexer_1_out), .sel(Ainvert));
  not not_2 (not_2_out, b);
  Multiplexer #(.enable("false")) multiplexer_2 (.in0(b), .in1(not_2_out), .out(multiplexer_2_out), .sel(Binvert));
  and and_1 (and_1_out, multiplexer_1_out, multiplexer_2_out);
  or or_1 (or_1_out, multiplexer_1_out, multiplexer_2_out);
  Adder #(.width(1)) adder_1 (.a(multiplexer_1_out), .b(multiplexer_2_out), .out(Set), .cin(CarryIn), .cout(CarryOut));
  Multiplexer #(.select(2), .enable("false")) multiplexer_3 (
    .in0(and_1_out), .in1(or_1_out), .in2(Set), .in3(Less), .out(Result), .sel(Operation));
endmodule

module sixteen_bit_ALU (
  input  [3:0] ALUOperation,
  input  [15:0] a,
  input  [15:0] b,
  output Zero,
  output [15:0] Result,
  output Overflow
);

  wire one_bit_alu_1_carryout, one_bit_alu_2_carryout, one_bit_alu_3_carryout, one_bit_alu_4_carryout,
       one_bit_alu_5_carryout, one_bit_alu_6_carryout, one_bit_alu_7_carryout, one_bit_alu_8_carryout,
       one_bit_alu_9_carryout, one_bit_alu_10_carryout, one_bit_alu_11_carryout, one_bit_alu_12_carryout,
       one_bit_alu_13_carryout, one_bit_alu_14_carryout, one_bit_alu_15_carryout, one_bit_alu_16_carryout,
       one_bit_alu_16_set, xor_1_out;

  one_bit_ALU one_bit_alu_1 (
    .a(a[0]), .b(b[0]), .Less(xor_1_out), .Ainvert(ALUOperation[3]), .Binvert(ALUOperation[2]),
    .CarryIn(ALUOperation[2]), .Operation(ALUOperation[1:0]), .CarryOut(one_bit_alu_1_carryout),
    .Result(Result[0]));  // open: Set
  one_bit_ALU one_bit_alu_2 (
    .a(a[1]), .b(b[1]), .Less(1'b0), .Ainvert(ALUOperation[3]), .Binvert(ALUOperation[2]),
    .CarryIn(one_bit_alu_1_carryout), .Operation(ALUOperation[1:0]), .CarryOut(one_bit_alu_2_carryout),
    .Result(Result[1]));  // open: Set
  one_bit_ALU one_bit_alu_3 (
    .a(a[2]), .b(b[2]), .Less(1'b0), .Ainvert(ALUOperation[3]), .Binvert(ALUOperation[2]),
    .CarryIn(one_bit_alu_2_carryout), .Operation(ALUOperation[1:0]), .CarryOut(one_bit_alu_3_carryout),
    .Result(Result[2]));  // open: Set
  one_bit_ALU one_bit_alu_4 (
    .a(a[3]), .b(b[3]), .Less(1'b0), .Ainvert(ALUOperation[3]), .Binvert(ALUOperation[2]),
    .CarryIn(one_bit_alu_3_carryout), .Operation(ALUOperation[1:0]), .CarryOut(one_bit_alu_4_carryout),
    .Result(Result[3]));  // open: Set
  one_bit_ALU one_bit_alu_5 (
    .a(a[4]), .b(b[4]), .Less(1'b0), .Ainvert(ALUOperation[3]), .Binvert(ALUOperation[2]),
    .CarryIn(one_bit_alu_4_carryout), .Operation(ALUOperation[1:0]), .CarryOut(one_bit_alu_5_carryout),
    .Result(Result[4]));  // open: Set
  one_bit_ALU one_bit_alu_6 (
    .a(a[5]), .b(b[5]), .Less(1'b0), .Ainvert(ALUOperation[3]), .Binvert(ALUOperation[2]),
    .CarryIn(one_bit_alu_5_carryout), .Operation(ALUOperation[1:0]), .CarryOut(one_bit_alu_6_carryout),
    .Result(Result[5]));  // open: Set
  one_bit_ALU one_bit_alu_7 (
    .a(a[6]), .b(b[6]), .Less(1'b0), .Ainvert(ALUOperation[3]), .Binvert(ALUOperation[2]),
    .CarryIn(one_bit_alu_6_carryout), .Operation(ALUOperation[1:0]), .CarryOut(one_bit_alu_7_carryout),
    .Result(Result[6]));  // open: Set
  one_bit_ALU one_bit_alu_8 (
    .a(a[7]), .b(b[7]), .Less(1'b0), .Ainvert(ALUOperation[3]), .Binvert(ALUOperation[2]),
    .CarryIn(one_bit_alu_7_carryout), .Operation(ALUOperation[1:0]), .CarryOut(one_bit_alu_8_carryout),
    .Result(Result[7]));  // open: Set
  one_bit_ALU one_bit_alu_9 (
    .a(a[8]), .b(b[8]), .Less(1'b0), .Ainvert(ALUOperation[3]), .Binvert(ALUOperation[2]),
    .CarryIn(one_bit_alu_8_carryout), .Operation(ALUOperation[1:0]), .CarryOut(one_bit_alu_9_carryout),
    .Result(Result[8]));  // open: Set
  one_bit_ALU one_bit_alu_10 (
    .a(a[9]), .b(b[9]), .Less(1'b0), .Ainvert(ALUOperation[3]), .Binvert(ALUOperation[2]),
    .CarryIn(one_bit_alu_9_carryout), .Operation(ALUOperation[1:0]), .CarryOut(one_bit_alu_10_carryout),
    .Result(Result[9]));  // open: Set
  one_bit_ALU one_bit_alu_11 (
    .a(a[10]), .b(b[10]), .Less(1'b0), .Ainvert(ALUOperation[3]), .Binvert(ALUOperation[2]),
    .CarryIn(one_bit_alu_10_carryout), .Operation(ALUOperation[1:0]), .CarryOut(one_bit_alu_11_carryout),
    .Result(Result[10]));  // open: Set
  one_bit_ALU one_bit_alu_12 (
    .a(a[11]), .b(b[11]), .Less(1'b0), .Ainvert(ALUOperation[3]), .Binvert(ALUOperation[2]),
    .CarryIn(one_bit_alu_11_carryout), .Operation(ALUOperation[1:0]), .CarryOut(one_bit_alu_12_carryout),
    .Result(Result[11]));  // open: Set
  one_bit_ALU one_bit_alu_13 (
    .a(a[12]), .b(b[12]), .Less(1'b0), .Ainvert(ALUOperation[3]), .Binvert(ALUOperation[2]),
    .CarryIn(one_bit_alu_12_carryout), .Operation(ALUOperation[1:0]), .CarryOut(one_bit_alu_13_carryout),
    .Result(Result[12]));  // open: Set
  one_bit_ALU one_bit_alu_14 (
    .a(a[13]), .b(b[13]), .Less(1'b0), .Ainvert(ALUOperation[3]), .Binvert(ALUOperation[2]),
    .CarryIn(one_bit_alu_13_carryout), .Operation(ALUOperation[1:0]), .CarryOut(one_bit_alu_14_carryout),
    .Result(Result[13]));  // open: Set
  one_bit_ALU one_bit_alu_15 (
    .a(a[14]), .b(b[14]), .Less(1'b0), .Ainvert(ALUOperation[3]), .Binvert(ALUOperation[2]),
    .CarryIn(one_bit_alu_14_carryout), .Operation(ALUOperation[1:0]), .CarryOut(one_bit_alu_15_carryout),
    .Result(Result[14]));  // open: Set
  one_bit_ALU one_bit_alu_16 (
    .a(a[15]), .b(b[15]), .Less(1'b0), .Ainvert(ALUOperation[3]), .Binvert(ALUOperation[2]),
    .CarryIn(one_bit_alu_15_carryout), .Operation(ALUOperation[1:0]), .CarryOut(one_bit_alu_16_carryout),
    .Result(Result[15]), .Set(one_bit_alu_16_set));
  xor xor_1 (xor_1_out, one_bit_alu_16_set, Overflow);
  xor xor_2 (Overflow, one_bit_alu_15_carryout, one_bit_alu_16_carryout);
  nor nor_1 (Zero, Result[0], Result[1], Result[2], Result[3], Result[4], Result[5], Result[6], Result[7], Result[8], Result[9], Result[10], Result[11], Result[12], Result[13], Result[14], Result[15]);
endmodule

module PCDecoder (
  input  [3:0] Opcode,
  input  Subop,
  input  Zero,
  input  Less,
  output RegtoPC,
  output IMMtoPC,
  output ZerosToALU,
  output [3:0] ALUOp
);

  wire and_4_out, and_5_out, and_6_out, and_7_out, and_8_out, not_1_out, not_2_out, not_3_out, not_4_out,
       not_5_out, not_6_out, not_7_out, not_8_out, not_9_out, not_10_out, not_11_out, not_12_out, not_13_out,
       not_14_out, not_15_out, not_16_out;

  not not_1 (not_1_out, Opcode[2]);
  not not_2 (not_2_out, Opcode[1]);
  not not_3 (not_3_out, Subop);
  not not_4 (not_4_out, Opcode[2]);
  not not_5 (not_5_out, Opcode[1]);
  not not_6 (not_6_out, Opcode[0]);
  not not_7 (not_7_out, Opcode[2]);
  not not_8 (not_8_out, Opcode[1]);
  not not_9 (not_9_out, Zero);
  not not_10 (not_10_out, Opcode[2]);
  not not_11 (not_11_out, Zero);
  not not_12 (not_12_out, Opcode[0]);
  not not_13 (not_13_out, Zero);
  not not_14 (not_14_out, Less);
  not not_15 (not_15_out, Opcode[0]);
  and and_1 (ZerosToALU, Opcode[3], not_16_out);
  not not_16 (not_16_out, Opcode[2]);
  and and_2 (ALUOp[1], Opcode[3], not_1_out);
  and and_3 (RegtoPC, Opcode[3], Opcode[2], not_2_out, Opcode[0], not_3_out);
  and and_4 (and_4_out, Opcode[3], not_4_out, not_5_out, not_6_out, Zero);
  and and_5 (and_5_out, Opcode[3], not_7_out, not_8_out, Opcode[0], not_9_out);
  and and_6 (and_6_out, Opcode[3], not_10_out, Opcode[0], not_11_out, Less);
  and and_7 (and_7_out, Opcode[3], Opcode[1], not_12_out, not_13_out, not_14_out);
  and and_8 (and_8_out, Opcode[3], Opcode[2], Opcode[1], not_15_out);
  or or_1 (IMMtoPC, and_4_out, and_5_out, and_6_out, and_7_out, and_8_out);

  assign {ALUOp[3:2], ALUOp[0]} = 3'b000;
endmodule

module PCDecoderLogic (
  input  Opcode3,
  input  Opcode2,
  input  Opcode1,
  input  Opcode0,
  input  Subop,
  input  Zero,
  input  Less,
  output RegtoPC,
  output IMMtoPC,
  output OnestoALU
);

  wire and_2_out, and_3_out, and_4_out, and_5_out, and_6_out, not_1_out, not_2_out, not_3_out, not_4_out,
       not_5_out, not_6_out, not_7_out, not_8_out, not_9_out, not_10_out, not_11_out, not_12_out, not_13_out,
       not_14_out, not_15_out;

  not not_1 (not_1_out, Opcode1);
  not not_2 (not_2_out, Subop);
  not not_3 (not_3_out, Opcode2);
  not not_4 (not_4_out, Opcode1);
  not not_5 (not_5_out, Opcode0);
  not not_6 (not_6_out, Opcode2);
  not not_7 (not_7_out, Opcode1);
  not not_8 (not_8_out, Zero);
  not not_9 (not_9_out, Opcode2);
  not not_10 (not_10_out, Zero);
  not not_11 (not_11_out, Opcode0);
  not not_12 (not_12_out, Zero);
  not not_13 (not_13_out, Less);
  not not_14 (not_14_out, Opcode0);
  not not_15 (not_15_out, Opcode2);
  and and_1 (RegtoPC, Opcode3, Opcode2, not_1_out, Opcode0, not_2_out);
  and and_2 (and_2_out, Opcode3, not_3_out, not_4_out, not_5_out, Zero);
  and and_3 (and_3_out, Opcode3, not_6_out, not_7_out, Opcode0, not_8_out);
  and and_4 (and_4_out, Opcode3, not_9_out, Opcode0, not_10_out, Less);
  and and_5 (and_5_out, Opcode3, Opcode1, not_11_out, not_12_out, not_13_out);
  and and_6 (and_6_out, Opcode3, Opcode2, Opcode1, not_14_out);
  and and_7 (OnestoALU, Opcode3, not_15_out);
  or or_1 (IMMtoPC, and_2_out, and_3_out, and_4_out, and_5_out, and_6_out);
endmodule

module Decoder (
  input  [3:0] Opcode,
  input  Subop,
  input  Zero,
  input  Less,
  output ShiftSrc,
  output ShifterToReg,
  output RegWrite,
  output [3:0] ALUOp,
  output IMMtoALU,
  output RegtoPC,
  output IMMtoPC,
  output ZerosToALU,
  output MemWrite,
  output MemtoReg,
  output Halt,
  output LED,
  output WriteLED,
  output MemRead,
  output PCtoReg
);

  wire Arith_LogDecoder_regwrite, JALDecoder_immtopc, JALDecoder_regwrite, MemDecoder_regwrite,
       PCDecoder_immtopc, ShifterDecoder_regwrite;
  wire [3:0] Arith_LogDecoder_aluoperation, PCDecoder_aluop;

  ShifterDecoder ShifterDecoder (
    .Opcode(Opcode), .ShiftSrc(ShiftSrc), .ShiftertoReg(ShifterToReg), .RegWrite(ShifterDecoder_regwrite));
  Arith_Log_Decoder Arith_LogDecoder (
    .Opcode(Opcode), .Subop(Subop), .ALUOperation(Arith_LogDecoder_aluoperation),
    .RegWrite(Arith_LogDecoder_regwrite), .ALUSrc(IMMtoALU));
  PCDecoder PCDecoder (
    .Opcode(Opcode), .Subop(Subop), .Zero(Zero), .Less(Less), .RegtoPC(RegtoPC), .IMMtoPC(PCDecoder_immtopc),
    .ZerosToALU(ZerosToALU), .ALUOp(PCDecoder_aluop));
  MemDecoder MemDecoder (
    .Opcode(Opcode), .Subop(Subop), .MemWrite(MemWrite), .MemtoReg(MemtoReg), .RegWrite(MemDecoder_regwrite),
    .MemRead(MemRead));
  HaltDecoder haltdecoder_1 (.Opcode(Opcode), .Halt(Halt), .LED(LED));
  PutDecoder PutDecoder (.Opcode(Opcode), .WriteLED(WriteLED));
  JALDecoder JALDecoder (
    .Opcode(Opcode), .IMMtoPC(JALDecoder_immtopc), .PCtoReg(PCtoReg), .RegWrite(JALDecoder_regwrite));
  or or_1 (RegWrite, ShifterDecoder_regwrite, Arith_LogDecoder_regwrite, MemDecoder_regwrite, JALDecoder_regwrite);
  or or_2 (IMMtoPC, PCDecoder_immtopc, JALDecoder_immtopc);
  assign ALUOp = Arith_LogDecoder_aluoperation | PCDecoder_aluop;  // OR_Gate or_3, 4 bits wide
endmodule

module MemDecoder (
  input  [3:0] Opcode,
  input  Subop,
  output MemWrite,
  output MemtoReg,
  output RegWrite,
  output MemRead
);

  and and_1 (MemWrite, ~Opcode[0], Opcode[1], Opcode[2], ~Opcode[3], Subop);  // AND_Gate
  and and_2 (MemRead, ~Opcode[0], Opcode[1], Opcode[2], ~Opcode[3], ~Subop);  // AND_Gate

  assign MemtoReg = MemRead;
  assign RegWrite = MemRead;
endmodule

module HaltDecoder (
  input  [3:0] Opcode,
  output Halt,
  output LED
);

  and and_1 (Halt, ~Opcode[3], Opcode[2], Opcode[1], Opcode[0]);  // AND_Gate

  assign LED = Halt;
endmodule

module PutDecoder (
  input  [3:0] Opcode,
  output WriteLED
);

  and and_1 (WriteLED, Opcode[0], Opcode[1], Opcode[2], Opcode[3]);
endmodule

module JALDecoder (
  input  [3:0] Opcode,
  output IMMtoPC,
  output PCtoReg,
  output RegWrite
);

  and and_1 (IMMtoPC, ~Opcode[0], ~Opcode[1], Opcode[2], Opcode[3]);  // AND_Gate

  assign PCtoReg = IMMtoPC;
  assign RegWrite = IMMtoPC;
endmodule

module ResultToLess (
  input  [15:0] Result,
  output Less
);


  assign Less = Result[15];
endmodule

module side (
  input  Op3,
  input  Op2,
  input  Op1,
  input  Op0,
  output Op3_2,
  output Op2_2,
  output Op1_2,
  output Op0_2
);

  wire not_1_out;

  and and_1 (Op1_2, Op3, not_1_out);
  not not_1 (not_1_out, Op2);

  assign Op0_2 = 1'b0;
  assign Op2_2 = 1'b0;
  assign Op3_2 = 1'b0;
endmodule

module ID_EX_Register (
  input  [15:0] ReadData1,
  input  [15:0] ReadData2,
  input  Clock,
  input  ID_EX_En,
  input  [2:0] WriteRegister,
  input  [15:0] SignExtImm,
  input  [3:0] ALUOp,
  input  [5:0] IF_ID_ControlSignals,
  input  [2:0] Rs1,
  input  [2:0] Rs2,
  output [15:0] ID_EX_ReadData1,
  output [15:0] ID_EX_ReadData2,
  output [2:0] ID_EX_WriteRegister,
  output [15:0] ID_EX_SignExtImm,
  output [3:0] ID_EX_ALUOp,
  output ID_EX_ALUSrc,
  output ID_EX_MemWrite,
  output ID_EX_MemRead,
  output ID_EX_MemToReg,
  output ID_EX_WriteEnable,
  output ID_EX_WriteLED,
  output [2:0] ID_EX_Rs1,
  output [2:0] ID_EX_Rs2
);

  Register #(.width(16)) register_1 (.D(ReadData1), .en(ID_EX_En), .Q(ID_EX_ReadData1), .clk(Clock));  // open: clr
  Register #(.width(16)) register_2 (.D(ReadData2), .en(ID_EX_En), .Q(ID_EX_ReadData2), .clk(Clock));  // open: clr
  Register #(.width(3)) u_WriteRegister (
    .D(WriteRegister), .en(ID_EX_En), .Q(ID_EX_WriteRegister), .clk(Clock));  // open: clr
  Register #(.width(16)) u_SignExtImm (.D(SignExtImm), .en(ID_EX_En), .Q(ID_EX_SignExtImm), .clk(Clock));  // open: clr
  Register #(.width(4)) u_ALUOp (.D(ALUOp), .en(ID_EX_En), .Q(ID_EX_ALUOp), .clk(Clock));  // open: clr
  Register #(.width(1)) ALUSrc (
    .D(IF_ID_ControlSignals[0]), .en(ID_EX_En), .Q(ID_EX_ALUSrc), .clk(Clock));  // open: clr
  Register #(.width(1)) MemWrite (
    .D(IF_ID_ControlSignals[1]), .en(ID_EX_En), .Q(ID_EX_MemWrite), .clk(Clock));  // open: clr
  Register #(.width(1)) MemRead (
    .D(IF_ID_ControlSignals[2]), .en(ID_EX_En), .Q(ID_EX_MemRead), .clk(Clock));  // open: clr
  Register #(.width(1)) MemToReg (
    .D(IF_ID_ControlSignals[3]), .en(ID_EX_En), .Q(ID_EX_MemToReg), .clk(Clock));  // open: clr
  Register #(.width(1)) WriteEnable (
    .D(IF_ID_ControlSignals[4]), .en(ID_EX_En), .Q(ID_EX_WriteEnable), .clk(Clock));  // open: clr
  Register #(.width(1)) WriteLED (
    .D(IF_ID_ControlSignals[5]), .en(ID_EX_En), .Q(ID_EX_WriteLED), .clk(Clock));  // open: clr
  Register #(.width(3)) u_Rs1 (.D(Rs1), .en(ID_EX_En), .Q(ID_EX_Rs1), .clk(Clock));  // open: clr
  Register #(.width(3)) u_Rs2 (.D(Rs2), .en(ID_EX_En), .Q(ID_EX_Rs2), .clk(Clock));  // open: clr
endmodule

module EX_MEM_Register (
  input  Clock,
  input  EX_MEM_En,
  input  [15:0] Result,
  input  [2:0] WriteRegister,
  input  [15:0] ReadData2,
  input  MemWrite,
  input  MemRead,
  input  MemToReg,
  input  WriteEnable,
  input  [2:0] Rs2,
  input  [15:0] ReadData1,
  output [15:0] EX_MEM_Result,
  output [2:0] EX_MEM_WriteRegister,
  output [15:0] EX_MEM_ReadData2,
  output EX_MEM_MemWrite,
  output EX_MEM_MemRead,
  output EX_MEM_MemToReg,
  output EX_MEM_WriteEnable,
  output [2:0] EX_MEM_Rs2,
  output [15:0] EX_MEM_ReadData1
);

  Register #(.width(16)) register_1 (.D(Result), .en(EX_MEM_En), .Q(EX_MEM_Result), .clk(Clock));  // open: clr
  Register #(.width(3)) u_WriteRegister (
    .D(WriteRegister), .en(EX_MEM_En), .Q(EX_MEM_WriteRegister), .clk(Clock));  // open: clr
  Register #(.width(16)) register_2 (.D(ReadData2), .en(EX_MEM_En), .Q(EX_MEM_ReadData2), .clk(Clock));  // open: clr
  Register #(.width(1)) u_MemWrite (.D(MemWrite), .en(EX_MEM_En), .Q(EX_MEM_MemWrite), .clk(Clock));  // open: clr
  Register #(.width(1)) u_MemRead (.D(MemRead), .en(EX_MEM_En), .Q(EX_MEM_MemRead), .clk(Clock));  // open: clr
  Register #(.width(1)) u_MemToReg (.D(MemToReg), .en(EX_MEM_En), .Q(EX_MEM_MemToReg), .clk(Clock));  // open: clr
  Register #(.width(1)) u_WriteEnable (
    .D(WriteEnable), .en(EX_MEM_En), .Q(EX_MEM_WriteEnable), .clk(Clock));  // open: clr
  Register #(.width(3)) u_Rs2 (.D(Rs2), .en(EX_MEM_En), .Q(EX_MEM_Rs2), .clk(Clock));  // open: clr
  Register #(.width(16)) register_3 (.D(ReadData1), .en(EX_MEM_En), .Q(EX_MEM_ReadData1), .clk(Clock));  // open: clr
endmodule

module MEM_WB_Register (
  input  Clock,
  input  [2:0] EX_MEM_WriteRegister,
  input  [15:0] Result,
  input  [15:0] EX_MEM_MemData,
  input  MemToReg,
  input  WriteEnable,
  output [2:0] MEM_WB_WriteRegister,
  output [15:0] MEM_WB_Result,
  output [15:0] MEM_WB_MemData,
  output MEM_WB_MemToReg,
  output MEM_WB_WriteEnable
);

  Register #(.width(3)) WriteRegister (
    .D(EX_MEM_WriteRegister), .en(1'b1), .Q(MEM_WB_WriteRegister), .clk(Clock));  // open: clr
  Register #(.width(16)) register_1 (.D(Result), .en(1'b1), .Q(MEM_WB_Result), .clk(Clock));  // open: clr
  Register #(.width(16)) register_2 (.D(EX_MEM_MemData), .en(1'b1), .Q(MEM_WB_MemData), .clk(Clock));  // open: clr
  Register #(.width(1)) u_MemToReg (.D(MemToReg), .en(1'b1), .Q(MEM_WB_MemToReg), .clk(Clock));  // open: clr
  Register #(.width(1)) u_WriteEnable (.D(WriteEnable), .en(1'b1), .Q(MEM_WB_WriteEnable), .clk(Clock));  // open: clr
endmodule

module ForwardingUnit (
  input  [2:0] Ex_Mem_RS1,
  input  [2:0] Ex_Mem_Rd,
  input  Ex_Mem_MemWrite,
  input  [2:0] IF_ID_RS1,
  input  Mem_WB_MemToReg,
  input  [2:0] IF_ID_RS2,
  input  Mem_WB_RegisterWrite,
  input  [2:0] ID_Ex_RS1,
  input  [2:0] Mem_WB_Rd,
  input  [2:0] ID_Ex_RS2,
  input  Ex_Mem_RegisterWrite,
  output C,
  output D,
  output E,
  output [1:0] A,
  output [1:0] B
);

  wire and_1_out, comparator_1_eq, comparator_2_eq, comparator_3_eq, comparator_4_eq, comparator_5_eq,
       comparator_6_eq, comparator_7_eq, comparator_8_eq, comparator_9_eq, comparator_10_eq,
       comparator_11_eq, not_1_out, not_2_out, not_3_out, not_4_out, not_5_out, not_6_out;

  Comparator #(.width(3)) comparator_1 (.a(ID_Ex_RS1), .b(3'b000), .eq(comparator_1_eq));  // open: gt, lt
  Comparator #(.width(3)) comparator_2 (.a(Ex_Mem_Rd), .b(ID_Ex_RS1), .eq(comparator_2_eq));  // open: gt, lt
  Comparator #(.width(3)) comparator_3 (.a(ID_Ex_RS1), .b(3'b000), .eq(comparator_3_eq));  // open: gt, lt
  Comparator #(.width(3)) comparator_4 (.a(Mem_WB_Rd), .b(ID_Ex_RS1), .eq(comparator_4_eq));  // open: gt, lt
  Comparator #(.width(3)) comparator_5 (.a(ID_Ex_RS2), .b(3'b000), .eq(comparator_5_eq));  // open: gt, lt
  Comparator #(.width(3)) comparator_6 (.a(Ex_Mem_Rd), .b(ID_Ex_RS2), .eq(comparator_6_eq));  // open: gt, lt
  Comparator #(.width(3)) comparator_7 (.a(ID_Ex_RS2), .b(3'b000), .eq(comparator_7_eq));  // open: gt, lt
  Comparator #(.width(3)) comparator_8 (.a(Mem_WB_Rd), .b(ID_Ex_RS2), .eq(comparator_8_eq));  // open: gt, lt
  not not_1 (not_1_out, comparator_1_eq);
  not not_2 (not_2_out, comparator_3_eq);
  not not_3 (not_3_out, comparator_5_eq);
  not not_4 (not_4_out, comparator_7_eq);
  Comparator #(.width(3)) comparator_9 (.a(Ex_Mem_RS1), .b(Mem_WB_Rd), .eq(comparator_9_eq));  // open: gt, lt
  and and_1 (and_1_out, Ex_Mem_MemWrite, Mem_WB_MemToReg);
  and and_2 (A[1], Ex_Mem_RegisterWrite, not_1_out, comparator_2_eq);
  and and_3 (B[1], Ex_Mem_RegisterWrite, not_3_out, comparator_6_eq);
  and and_4 (C, comparator_9_eq, and_1_out);
  not not_5 (not_5_out, A[1]);
  and and_5 (A[0], not_5_out, Mem_WB_RegisterWrite, not_2_out, comparator_4_eq);
  not not_6 (not_6_out, B[1]);
  and and_6 (B[0], not_6_out, Mem_WB_RegisterWrite, not_4_out, comparator_8_eq);
  Comparator #(.width(3)) comparator_10 (.a(Mem_WB_Rd), .b(IF_ID_RS1), .eq(comparator_10_eq));  // open: gt, lt
  Comparator #(.width(3)) comparator_11 (.a(Mem_WB_Rd), .b(IF_ID_RS2), .eq(comparator_11_eq));  // open: gt, lt
  and and_7 (D, comparator_10_eq, Mem_WB_RegisterWrite);
  and and_8 (E, comparator_11_eq, Mem_WB_RegisterWrite);
endmodule

module HazardControlUnit (
  input  IF_ID_MemWrite,
  input  ALUSrc,
  input  PCSrc,
  input  ID_Ex_MemRead,
  input  [2:0] ID_Ex_Rd,
  input  [2:0] IF_ID_RS1,
  input  [2:0] IF_ID_RS2,
  input  [2:0] Mem_WB_Rd,
  output Stall,
  output Flush
);

  wire comparator_1_eq, comparator_2_eq, or_1_out;

  Comparator #(.width(3)) comparator_1 (.a(ID_Ex_Rd), .b(IF_ID_RS1), .eq(comparator_1_eq));  // open: gt, lt
  Comparator #(.width(3)) comparator_2 (.a(ID_Ex_Rd), .b(IF_ID_RS2), .eq(comparator_2_eq));  // open: gt, lt
  or or_1 (or_1_out, comparator_1_eq, comparator_2_eq);
  and and_1 (Stall, or_1_out, ID_Ex_MemRead, ~IF_ID_MemWrite);  // AND_Gate

  assign Flush = PCSrc;
endmodule
